# Fritzing sketch alarm (saved by Fritzing 0.9.2b)
circuit board: 8.49489cm x 5.87022cm
breadboards: 1

parts:
  LED1 = LED - 5mm [color="Green (565nm)" part_number=LED_OPEN_DOOR_1 package="5 mm [THT]"]
  S2 = Reed switch [part_number=REED_SWITCH_1 package=THT]
  S1 = Pushbutton [part_number=Activator package="[THT]"]
  R1 = Resistor [tolerance=±5% resistance=820 package=THT]
  LED_ACTIVATE = LED - 5mm [color="Red (633nm)" package="5 mm [THT]"]
  R2 = Resistor [tolerance=±5% resistance=100 package=THT]
  Part1 = Arduino Uno (Rev3) [part_number=Arduino]
  J1 = Piezo Speaker [part_number=BUZZER]

nets (from the schematic view):
  N1: LED1.cathode, Part1.GND
  N2: LED1.anode, Part1.D13/SCK
  N3: S2.pin_1, Part1.D7
  N4: S2.pin_2, LED_ACTIVATE.cathode, Part1.3V3
  N5: S1.Pin_1, S1.Pin_2, R1.Pin_0, Part1.D2
  N6: S1.Pin_3, S1.Pin_4, Part1.5V
  N7: R1.Pin_1, R2.Pin_1, J1.pin2
  N8: LED_ACTIVATE.anode, R2.Pin_0, Part1.D8
  N9: Part1.D9_PWM, J1.pin1

// code stored in the sketch: alarm.ino
/*
  Home Alarm
  Model: 01
  
  Simple alarm using magnetic contactors for doors and windows
*/

const int REED_SWITCH_1 = 7;      // Magnetic contact
const int LED_OPEN_DOOR_1 = 8;    // LED to show door opened/closed
const int LED_ACTIVE = 13;        // LED to show when alarm is active
const int BUTTON_ACTIVATION = 2;  // Button to show when alarm is active
const int SOUND_SIGNAL = 9;       // Buzzer

int door_sensor = 0;              // will be used to store the state of the door (REED_SWITCH_1 input pin)
int old_door_sensor = 0;          // this variable stores the previous value of door_sensor

int activate = 0;                 // will be used to store the state activation (BUTTON_ACTIVATION input pin)
int old_activate = 0;             // this variable stores the previous value of "activate"
int active_state = 0;             // 0 = LED off while 1 = LED on

void setup() {
  pinMode(REED_SWITCH_1, INPUT);     // Set digital pin as input
  pinMode(LED_OPEN_DOOR_1, OUTPUT);  // Set digital pin as output
  
  pinMode(BUTTON_ACTIVATION, INPUT); // Set digital pin as input
  pinMode(LED_ACTIVE, OUTPUT);       // Set digital pin as output
  
  pinMode(SOUND_SIGNAL, OUTPUT);     // Set digital pin as output
  
  // PC output
  Serial.begin(9600);                // initialize serial communication at 9600 bits per second
}

void loop() {
  int door_sensor = digitalRead(REED_SWITCH_1);  // read the input pin

  if (door_sensor != old_door_sensor) {  // If door change it status, change LED
    // Since Magnetic Contact is inverse led should be high when it is low
    // door_sensor -> HIGH: Opened
    // door_sensor -> LOW: Closed
    if (door_sensor == 1) {
      digitalWrite(LED_OPEN_DOOR_1, HIGH);  // Turn LED ON
      if (active_state == 1) { // Since alarm is active turn on sound signal
        digitalWrite(SOUND_SIGNAL, HIGH);
      }
    } else {  // If door is closed turn off led
      digitalWrite(LED_OPEN_DOOR_1, LOW);  // Turn LED OFF
    }
  }
  
  old_door_sensor = door_sensor; // Save new door status
  
  int activate = digitalRead(BUTTON_ACTIVATION);  // read the input pin
  
  // Alarm Activation
  // check if the input is HIGH (button pressed) and change the state
  if ((activate == HIGH) && (activate != old_activate)) {
    active_state = 1 - active_state;
  }

  old_activate = activate;  // activate is now old, let's store it

  if (active_state == 1) {
    digitalWrite(LED_ACTIVE, HIGH); // turn LED ON
  } else {
    digitalWrite(LED_ACTIVE, LOW);
    digitalWrite(SOUND_SIGNAL, LOW); // Stop sound
  }
}
